# Fritzing sketch discordian_remote (saved by Fritzing 0.7.7b)
breadboards: 1

parts:
  Arduino1 = Arduino  # not connected
  Arduino_Ethernet_Shield1 = Arduino Ethernet Shield
  R1 = Resistor [tolerance=±5% resistance=330 package=THT]
  LED1 = LED - 5mm [color="Infrared (850nm)" package="5 mm [THT]"]
  J1 = Infrared Proximity Sensor

nets:
  N1: Arduino_Ethernet_Shield1.D7, J1.Vout
  N2: Arduino_Ethernet_Shield1.D3, LED1.anode
  +5V: Arduino_Ethernet_Shield1.+5V, J1.Vcc
  GND: Arduino_Ethernet_Shield1.GND, J1.GND
  N3: R1.Pin_0, LED1.cathode

notes:
  Beware that the motion sensor is NOT what I've used: Fritzing does not have the PIR sensor, yet.
  Also, I'm not too sure that the resistor was chosen wisely.
